# Fritzing sketch project 2 fritzing progress (saved by Fritzing 0.9.2b)
breadboards: 2

parts:
  R13 = Trimmer Potentiometer [maximum_resistance=10kΩ package=THT]
  LCD3 = LCD screen
  R14 = Resistor [tolerance=±5% resistance=220 package=THT]
  Part5 = Arduino Motor Shield (Rev3)
  J1 = Basic Servo
  J2 = Basic Servo
  KEYPAD1 = Membrane Matrix Keypad
  J3 = Piezo Speaker
  R16 = Resistor [tolerance=±5% resistance=330 package=THT]
  LED2 = smd LED [color="Red (633nm)" package="0603 [SMD]"]
  R17 = Resistor [tolerance=±5% resistance=220 package=THT]

nets:
  GND: R13.leg1, LCD3.R/W, LCD3.LED-, J1.gnd, J2.gnd
  N1: R13.wiper, LCD3.VDD
  VCC: R13.leg2, LCD3.VSS, R14.Pin_0, J1.vcc, J2.vcc
  N2: LCD3.RS, Part5.D13/DirB
  N3: LCD3.E, Part5.D12/DirA
  N4: LCD3.DB4, Part5.D11_PWM/B
  N5: LCD3.DB5, Part5.D10_PWM
  N6: LCD3.DB6, Part5.D8/BreakeB
  N7: LCD3.DB7, Part5.D7
  N8: LCD3.LED+, R14.Pin_1
  N9: Part5.A0, KEYPAD1.6
  N10: Part5.A1, KEYPAD1.5
  N11: Part5.A2, KEYPAD1.4
  N12: Part5.A3, KEYPAD1.3
  N13: Part5.A4, KEYPAD1.2
  N14: Part5.A5, KEYPAD1.1
  N15: Part5.D9/BreakeA, KEYPAD1.7
  N16: Part5.GND, J3.pin1, R17.Pin_0
  N17: Part5.IOREF, J1.pulse
  N18: Part5.D1/TX, J2.pulse
  N19: Part5.D3_PWM/A, R16.Pin_0
  N20: Part5.D4, LED2.anode
  N21: J3.pin2, R16.Pin_1
  N22: LED2.cathode, R17.Pin_1

custom parts:
  Membrane Matrix Keypad: Membrane Matrix 3x4 Keypad
